// Logisim project NIA-BR32.circ as structural Verilog: 2 circuits, main circuit BR4
module BR4 (
  input  RegWR,
  input  [1:0] RA,
  input  [1:0] RB,
  input  CLEAR,
  input  [1:0] RW,
  input  [31:0] busW,
  input  clk,
  output [31:0] busA,
  output [31:0] busB
);

  wire and_1_out, and_2_out, and_3_out, and_4_out, decoder_1_out0, decoder_1_out1, decoder_1_out2,
       decoder_1_out3;
  wire [31:0] register_1_q, register_2_q, register_3_q, register_4_q;

  Decoder #(.select(2), .enable("false")) decoder_1 (
    .out0(decoder_1_out0), .out1(decoder_1_out1), .out2(decoder_1_out2), .out3(decoder_1_out3), .sel(RW));
  and and_1 (and_1_out, RegWR, decoder_1_out0);
  and and_2 (and_2_out, RegWR, decoder_1_out1);
  and and_3 (and_3_out, RegWR, decoder_1_out2);
  and and_4 (and_4_out, RegWR, decoder_1_out3);
  Register #(.width(32)) register_1 (.D(busW), .en(and_1_out), .Q(register_1_q), .clk(clk), .clr(CLEAR));
  Register #(.width(32)) register_2 (.D(busW), .en(and_2_out), .Q(register_2_q), .clk(clk), .clr(CLEAR));
  Register #(.width(32)) register_3 (.D(busW), .en(and_3_out), .Q(register_3_q), .clk(clk), .clr(CLEAR));
  Register #(.width(32)) register_4 (.D(busW), .en(and_4_out), .Q(register_4_q), .clk(clk), .clr(CLEAR));
  Multiplexer #(.select(2), .width(32), .enable("false")) multiplexer_1 (
    .in0(register_1_q), .in1(register_2_q), .in2(register_3_q), .in3(register_4_q), .out(busA), .sel(RA));
  Multiplexer #(.select(2), .width(32), .enable("false")) multiplexer_2 (
    .in0(register_1_q), .in1(register_2_q), .in2(register_3_q), .in3(register_4_q), .out(busB), .sel(RB));
endmodule

module BR32 (
  input  [31:0] busW,
  input  RegWr,
  input  [4:0] RA,
  input  [4:0] RB,
  input  [4:0] RW,
  output [31:0] out_6,
  output [31:0] out_7
);

  wire CLEAR_out, clock_1_out, decoder_1_out0, decoder_1_out1, decoder_1_out2, decoder_1_out3,
       decoder_1_out4, decoder_1_out5, decoder_1_out6, decoder_1_out7;
  wire [31:0] br4_1_busa, br4_1_busb, br4_2_busa, br4_2_busb, br4_3_busa, br4_3_busb, br4_4_busa, br4_4_busb,
       br4_5_busa, br4_5_busb, br4_6_busa, br4_6_busb, br4_7_busa, br4_7_busb, br4_8_busa;

  Decoder #(.select(3), .disabled(0)) decoder_1 (
    .out0(decoder_1_out0), .out1(decoder_1_out1), .out2(decoder_1_out2), .out3(decoder_1_out3),
    .out4(decoder_1_out4), .out5(decoder_1_out5), .out6(decoder_1_out6), .out7(decoder_1_out7),
    .sel(RW[4:2]), .en(RegWr));
  Clock clock_1 (.out(clock_1_out));
  BR4 br4_1 (
    .RegWR(decoder_1_out0), .RW(RW[1:0]), .busW(busW), .busA(br4_1_busa), .busB(br4_1_busb), .RA(RA[1:0]),
    .RB(RB[1:0]), .clk(clock_1_out), .CLEAR(CLEAR_out));
  BR4 br4_2 (
    .RegWR(decoder_1_out1), .RW(RW[1:0]), .busW(busW), .busA(br4_2_busa), .busB(br4_2_busb), .RA(RA[1:0]),
    .RB(RB[1:0]), .clk(clock_1_out), .CLEAR(CLEAR_out));
  BR4 br4_3 (
    .RegWR(decoder_1_out2), .RW(RW[1:0]), .busW(busW), .busA(br4_3_busa), .busB(br4_3_busb), .RA(RA[1:0]),
    .RB(RB[1:0]), .clk(clock_1_out), .CLEAR(CLEAR_out));
  BR4 br4_4 (
    .RegWR(decoder_1_out3), .RW(RW[1:0]), .busW(busW), .busA(br4_4_busa), .busB(br4_4_busb), .RA(RA[1:0]),
    .RB(RB[1:0]), .clk(clock_1_out), .CLEAR(CLEAR_out));
  BR4 br4_5 (
    .RegWR(decoder_1_out4), .RW(RW[1:0]), .busW(busW), .busA(br4_5_busa), .busB(br4_5_busb), .RA(RA[1:0]),
    .RB(RB[1:0]), .clk(clock_1_out), .CLEAR(CLEAR_out));
  BR4 br4_6 (
    .RegWR(decoder_1_out5), .RW(RW[1:0]), .busW(busW), .busA(br4_6_busa), .busB(br4_6_busb), .RA(RA[1:0]),
    .RB(RB[1:0]), .clk(clock_1_out), .CLEAR(CLEAR_out));
  BR4 br4_7 (
    .RegWR(decoder_1_out6), .RW(RW[1:0]), .busW(busW), .busA(br4_7_busa), .busB(br4_7_busb), .RA(RA[1:0]),
    .RB(RB[1:0]), .clk(clock_1_out), .CLEAR(CLEAR_out));
  BR4 br4_8 (
    .RegWR(decoder_1_out7), .RW(RW[1:0]), .busW(busW), .busA(br4_8_busa), .busB(br4_8_busa), .RA(RA[1:0]),
    .RB(RB[1:0]), .clk(clock_1_out), .CLEAR(CLEAR_out));
  Button CLEAR (.out(CLEAR_out));
  Multiplexer #(.select(3), .width(32), .enable("false")) multiplexer_1 (
    .in0(br4_1_busa), .in1(br4_2_busa), .in2(br4_3_busa), .in3(br4_4_busa), .in4(br4_5_busa),
    .in5(br4_6_busa), .in6(br4_7_busa), .in7(br4_8_busa), .out(out_6), .sel(RA[4:2]));
  Multiplexer #(.select(3), .width(32), .enable("false")) multiplexer_2 (
    .in0(br4_1_busb), .in1(br4_2_busb), .in2(br4_3_busb), .in3(br4_4_busb), .in4(br4_5_busb),
    .in5(br4_6_busb), .in6(br4_7_busb), .in7(br4_8_busa), .out(out_7), .sel(RB[4:2]));
endmodule
