// Logisim project NIA-multi.circ as structural Verilog: 3 circuits, main circuit BR4
module BR4 (
  input  RegWR,
  input  [1:0] RA,
  input  [1:0] RB,
  input  CLEAR,
  input  [1:0] RW,
  input  [31:0] busW,
  input  clk,
  output [31:0] busA,
  output [31:0] busB
);

  wire and_1_out, and_2_out, and_3_out, and_4_out, decoder_1_out0, decoder_1_out1, decoder_1_out2,
       decoder_1_out3;
  wire [31:0] register_1_q, register_2_q, register_3_q, register_4_q;

  Decoder #(.select(2), .enable("false")) decoder_1 (
    .out0(decoder_1_out0), .out1(decoder_1_out1), .out2(decoder_1_out2), .out3(decoder_1_out3), .sel(RW));
  and and_1 (and_1_out, RegWR, decoder_1_out0);
  and and_2 (and_2_out, RegWR, decoder_1_out1);
  and and_3 (and_3_out, RegWR, decoder_1_out2);
  and and_4 (and_4_out, RegWR, decoder_1_out3);
  Register #(.width(32)) register_1 (.D(busW), .en(and_1_out), .Q(register_1_q), .clk(clk), .clr(CLEAR));
  Register #(.width(32)) register_2 (.D(busW), .en(and_2_out), .Q(register_2_q), .clk(clk), .clr(CLEAR));
  Register #(.width(32)) register_3 (.D(busW), .en(and_3_out), .Q(register_3_q), .clk(clk), .clr(CLEAR));
  Register #(.width(32)) register_4 (.D(busW), .en(and_4_out), .Q(register_4_q), .clk(clk), .clr(CLEAR));
  Multiplexer #(.select(2), .width(32), .enable("false")) multiplexer_1 (
    .in0(register_1_q), .in1(register_2_q), .in2(register_3_q), .in3(register_4_q), .out(busA), .sel(RA));
  Multiplexer #(.select(2), .width(32), .enable("false")) multiplexer_2 (
    .in0(register_1_q), .in1(register_2_q), .in2(register_3_q), .in3(register_4_q), .out(busB), .sel(RB));
endmodule

module BR32 (
  input  [31:0] busW,
  input  RegWr,
  input  [4:0] RA,
  input  [4:0] RB,
  input  [4:0] RW,
  input  CLK,
  output [31:0] busA,
  output [31:0] busB
);

  wire CLEAR_out, decoder_1_out0, decoder_1_out1, decoder_1_out2, decoder_1_out3, decoder_1_out4,
       decoder_1_out5, decoder_1_out6, decoder_1_out7;
  wire [31:0] br4_1_busa, br4_1_busb, br4_2_busa, br4_2_busb, br4_3_busa, br4_3_busb, br4_4_busa, br4_4_busb,
       br4_5_busa, br4_5_busb, br4_6_busa, br4_6_busb, br4_7_busa, br4_7_busb, br4_8_busa;

  Decoder #(.select(3), .disabled(0)) decoder_1 (
    .out0(decoder_1_out0), .out1(decoder_1_out1), .out2(decoder_1_out2), .out3(decoder_1_out3),
    .out4(decoder_1_out4), .out5(decoder_1_out5), .out6(decoder_1_out6), .out7(decoder_1_out7),
    .sel(RW[4:2]), .en(RegWr));
  BR4 br4_1 (
    .RegWR(decoder_1_out0), .RW(RW[1:0]), .busW(busW), .busA(br4_1_busa), .busB(br4_1_busb), .RA(RA[1:0]),
    .RB(RB[1:0]), .clk(CLK), .CLEAR(CLEAR_out));
  BR4 br4_2 (
    .RegWR(decoder_1_out1), .RW(RW[1:0]), .busW(busW), .busA(br4_2_busa), .busB(br4_2_busb), .RA(RA[1:0]),
    .RB(RB[1:0]), .clk(CLK), .CLEAR(CLEAR_out));
  BR4 br4_3 (
    .RegWR(decoder_1_out2), .RW(RW[1:0]), .busW(busW), .busA(br4_3_busa), .busB(br4_3_busb), .RA(RA[1:0]),
    .RB(RB[1:0]), .clk(CLK), .CLEAR(CLEAR_out));
  BR4 br4_4 (
    .RegWR(decoder_1_out3), .RW(RW[1:0]), .busW(busW), .busA(br4_4_busa), .busB(br4_4_busb), .RA(RA[1:0]),
    .RB(RB[1:0]), .clk(CLK), .CLEAR(CLEAR_out));
  BR4 br4_5 (
    .RegWR(decoder_1_out4), .RW(RW[1:0]), .busW(busW), .busA(br4_5_busa), .busB(br4_5_busb), .RA(RA[1:0]),
    .RB(RB[1:0]), .clk(CLK), .CLEAR(CLEAR_out));
  BR4 br4_6 (
    .RegWR(decoder_1_out5), .RW(RW[1:0]), .busW(busW), .busA(br4_6_busa), .busB(br4_6_busb), .RA(RA[1:0]),
    .RB(RB[1:0]), .clk(CLK), .CLEAR(CLEAR_out));
  BR4 br4_7 (
    .RegWR(decoder_1_out6), .RW(RW[1:0]), .busW(busW), .busA(br4_7_busa), .busB(br4_7_busb), .RA(RA[1:0]),
    .RB(RB[1:0]), .clk(CLK), .CLEAR(CLEAR_out));
  BR4 br4_8 (
    .RegWR(decoder_1_out7), .RW(RW[1:0]), .busW(busW), .busA(br4_8_busa), .busB(br4_8_busa), .RA(RA[1:0]),
    .RB(RB[1:0]), .clk(CLK), .CLEAR(CLEAR_out));
  Button CLEAR (.out(CLEAR_out));
  Multiplexer #(.select(3), .width(32), .enable("false")) multiplexer_1 (
    .in0(br4_1_busa), .in1(br4_2_busa), .in2(br4_3_busa), .in3(br4_4_busa), .in4(br4_5_busa),
    .in5(br4_6_busa), .in6(br4_7_busa), .in7(br4_8_busa), .out(busA), .sel(RA[4:2]));
  Multiplexer #(.select(3), .width(32), .enable("false")) multiplexer_2 (
    .in0(br4_1_busb), .in1(br4_2_busb), .in2(br4_3_busb), .in3(br4_4_busb), .in4(br4_5_busb),
    .in5(br4_6_busb), .in6(br4_7_busb), .in7(br4_8_busa), .out(busB), .sel(RB[4:2]));
endmodule

module CPU (
);

  wire button_1_out, clock_1_out;
  wire [2:0] rom_2_data;
  wire [3:0] register_1_q;
  wire [5:0] rom_3_data;
  wire [7:0] counter_1_q;
  wire [20:0] rom_1_data;
  wire [31:0] adder_1_out, bit_extender_1_out, br32_1_busa, br32_1_busb, multiplexer_1_out, RA_q, RB_q, RC_q;

  Counter counter_1 (
    .count(rom_3_data[5]), .Q(counter_1_q), .clk(clock_1_out), .clr(button_1_out));  // open: load, D, carry
  Button button_1 (.out(button_1_out));
  Clock clock_1 (.out(clock_1_out));
  ROM #(.dataWidth(22)) rom_1 (.addr(counter_1_q), .data({register_1_q[0], rom_1_data}));  // open: sel
  ROM #(.addrWidth(4), .dataWidth(3)) rom_2 (.addr(register_1_q), .data(rom_2_data));  // open: sel
  Register #(.width(3)) register_1 (.D(rom_2_data), .Q(register_1_q[3:1]), .clk(clock_1_out));  // open: en, clr
  BR32 br32_1 (
    .busW(multiplexer_1_out), .RegWr(rom_3_data[0]), .RA(rom_1_data[15:11]), .RB(rom_1_data[10:6]),
    .RW(rom_1_data[20:16]), .busA(br32_1_busa), .busB(br32_1_busb), .CLK(clock_1_out));
  assign bit_extender_1_out = {{16{rom_1_data[15]}}, rom_1_data[15:0]};  // Bit_Extender bit_extender_1
  Register #(.width(32)) RA (.D(br32_1_busa), .en(rom_3_data[2]), .Q(RA_q), .clk(clock_1_out));  // open: clr
  Register #(.width(32)) RB (.D(br32_1_busb), .en(rom_3_data[1]), .Q(RB_q), .clk(clock_1_out));  // open: clr
  ROM #(.addrWidth(3), .dataWidth(6)) rom_3 (.addr(register_1_q[3:1]), .data(rom_3_data));  // open: sel
  Adder #(.width(32)) adder_1 (.a(RA_q), .b(RB_q), .out(adder_1_out));  // open: cin, cout
  Multiplexer #(.width(32), .enable("false")) multiplexer_1 (
    .in0(bit_extender_1_out), .in1(RC_q), .out(multiplexer_1_out), .sel(rom_3_data[4]));
  Register #(.width(32)) RC (.D(adder_1_out), .en(rom_3_data[3]), .Q(RC_q), .clk(clock_1_out));  // open: clr

  // Notes on the sheet:
  //   contents of rom_1 (hex, n*v repeats v):
  //   7 10003 20009 30002 40007 50004 260040 261180 261980 262180 262980
  //   contents of rom_2 (hex, n*v repeats v):
  //   1 2 0 0 3 3 4 4
  //   CONTROL UNIT
  //   contents of rom_3 (hex, n*v repeats v):
  //   0 21 6 18 31
  //   CLOCK CABLE
endmodule
