// Logisim project NIA-multi2.circ as structural Verilog: 3 circuits, main circuit BR4
module BR4 (
  input  RegWR,
  input  [1:0] RA,
  input  [1:0] RB,
  input  CLEAR,
  input  [1:0] RW,
  input  [31:0] busW,
  input  clk,
  output [31:0] busA,
  output [31:0] busB
);

  wire and_1_out, and_2_out, and_3_out, and_4_out, decoder_1_out0, decoder_1_out1, decoder_1_out2,
       decoder_1_out3;
  wire [31:0] register_1_q, register_2_q, register_3_q, register_4_q;

  Decoder #(.select(2), .enable("false")) decoder_1 (
    .out0(decoder_1_out0), .out1(decoder_1_out1), .out2(decoder_1_out2), .out3(decoder_1_out3), .sel(RW));
  and and_1 (and_1_out, RegWR, decoder_1_out0);
  and and_2 (and_2_out, RegWR, decoder_1_out1);
  and and_3 (and_3_out, RegWR, decoder_1_out2);
  and and_4 (and_4_out, RegWR, decoder_1_out3);
  Register #(.width(32)) register_1 (.D(busW), .en(and_1_out), .Q(register_1_q), .clk(clk), .clr(CLEAR));
  Register #(.width(32)) register_2 (.D(busW), .en(and_2_out), .Q(register_2_q), .clk(clk), .clr(CLEAR));
  Register #(.width(32)) register_3 (.D(busW), .en(and_3_out), .Q(register_3_q), .clk(clk), .clr(CLEAR));
  Register #(.width(32)) register_4 (.D(busW), .en(and_4_out), .Q(register_4_q), .clk(clk), .clr(CLEAR));
  Multiplexer #(.select(2), .width(32), .enable("false")) multiplexer_1 (
    .in0(register_1_q), .in1(register_2_q), .in2(register_3_q), .in3(register_4_q), .out(busA), .sel(RA));
  Multiplexer #(.select(2), .width(32), .enable("false")) multiplexer_2 (
    .in0(register_1_q), .in1(register_2_q), .in2(register_3_q), .in3(register_4_q), .out(busB), .sel(RB));
endmodule

module BR32 (
  input  [31:0] busW,
  input  RegWr,
  input  [4:0] RA,
  input  [4:0] RB,
  input  [4:0] RW,
  input  CLK,
  output [31:0] busA,
  output [31:0] busB
);

  wire CLEAR_out, decoder_1_out0, decoder_1_out1, decoder_1_out2, decoder_1_out3, decoder_1_out4,
       decoder_1_out5, decoder_1_out6, decoder_1_out7;
  wire [31:0] br4_1_busa, br4_1_busb, br4_2_busa, br4_2_busb, br4_3_busa, br4_3_busb, br4_4_busa, br4_4_busb,
       br4_5_busa, br4_5_busb, br4_6_busa, br4_6_busb, br4_7_busa, br4_7_busb, br4_8_busa;

  Decoder #(.select(3), .disabled(0)) decoder_1 (
    .out0(decoder_1_out0), .out1(decoder_1_out1), .out2(decoder_1_out2), .out3(decoder_1_out3),
    .out4(decoder_1_out4), .out5(decoder_1_out5), .out6(decoder_1_out6), .out7(decoder_1_out7),
    .sel(RW[4:2]), .en(RegWr));
  BR4 br4_1 (
    .RegWR(decoder_1_out0), .RW(RW[1:0]), .busW(busW), .busA(br4_1_busa), .busB(br4_1_busb), .RA(RA[1:0]),
    .RB(RB[1:0]), .clk(CLK), .CLEAR(CLEAR_out));
  BR4 br4_2 (
    .RegWR(decoder_1_out1), .RW(RW[1:0]), .busW(busW), .busA(br4_2_busa), .busB(br4_2_busb), .RA(RA[1:0]),
    .RB(RB[1:0]), .clk(CLK), .CLEAR(CLEAR_out));
  BR4 br4_3 (
    .RegWR(decoder_1_out2), .RW(RW[1:0]), .busW(busW), .busA(br4_3_busa), .busB(br4_3_busb), .RA(RA[1:0]),
    .RB(RB[1:0]), .clk(CLK), .CLEAR(CLEAR_out));
  BR4 br4_4 (
    .RegWR(decoder_1_out3), .RW(RW[1:0]), .busW(busW), .busA(br4_4_busa), .busB(br4_4_busb), .RA(RA[1:0]),
    .RB(RB[1:0]), .clk(CLK), .CLEAR(CLEAR_out));
  BR4 br4_5 (
    .RegWR(decoder_1_out4), .RW(RW[1:0]), .busW(busW), .busA(br4_5_busa), .busB(br4_5_busb), .RA(RA[1:0]),
    .RB(RB[1:0]), .clk(CLK), .CLEAR(CLEAR_out));
  BR4 br4_6 (
    .RegWR(decoder_1_out5), .RW(RW[1:0]), .busW(busW), .busA(br4_6_busa), .busB(br4_6_busb), .RA(RA[1:0]),
    .RB(RB[1:0]), .clk(CLK), .CLEAR(CLEAR_out));
  BR4 br4_7 (
    .RegWR(decoder_1_out6), .RW(RW[1:0]), .busW(busW), .busA(br4_7_busa), .busB(br4_7_busb), .RA(RA[1:0]),
    .RB(RB[1:0]), .clk(CLK), .CLEAR(CLEAR_out));
  BR4 br4_8 (
    .RegWR(decoder_1_out7), .RW(RW[1:0]), .busW(busW), .busA(br4_8_busa), .busB(br4_8_busa), .RA(RA[1:0]),
    .RB(RB[1:0]), .clk(CLK), .CLEAR(CLEAR_out));
  Button CLEAR (.out(CLEAR_out));
  Multiplexer #(.select(3), .width(32), .enable("false")) multiplexer_1 (
    .in0(br4_1_busa), .in1(br4_2_busa), .in2(br4_3_busa), .in3(br4_4_busa), .in4(br4_5_busa),
    .in5(br4_6_busa), .in6(br4_7_busa), .in7(br4_8_busa), .out(busA), .sel(RA[4:2]));
  Multiplexer #(.select(3), .width(32), .enable("false")) multiplexer_2 (
    .in0(br4_1_busb), .in1(br4_2_busb), .in2(br4_3_busb), .in3(br4_4_busb), .in4(br4_5_busb),
    .in5(br4_6_busb), .in6(br4_7_busb), .in7(br4_8_busa), .out(busB), .sel(RB[4:2]));
endmodule

module CPU (
  output [31:0] out_1,
  output [15:0] out_2,
  output [15:0] out_3,
  output [31:0] out_4,
  output [4:0] RA,
  output [4:0] RD,
  output [4:0] RB,
  output [2:0] out_8
);

  wire and_1_out, button_1_out, clock_1_out, not_1_out, not_2_out;
  wire [0:0] comparator_1_eq;
  wire [4:0] register_1_q, rom_2_data;
  wire [6:0] RB_q;
  wire [12:0] rom_3_data;
  wire [15:0] COUNTER_q;
  wire [18:16] IR_q;
  wire [31:0] bit_extender_1_out, br32_1_busa, br32_1_busb, multiplexer_3_out, ram_1_data, RC_q, RMEM_q,
       rom_1_data;
  wire [31:7] RB_q_2;
  wire [31:16] RA_q;

  Counter #(.width(16), .max('hffff)) COUNTER (
    .load(rom_3_data[2]), .D(out_2), .count(rom_3_data[4]), .Q(COUNTER_q), .clk(clock_1_out),
    .clr(button_1_out));  // open: carry
  Clock clock_1 (.out(clock_1_out));
  Button button_1 (.out(button_1_out));
  ROM #(.addrWidth(16), .dataWidth(32)) rom_1 (.addr(COUNTER_q), .data(rom_1_data));  // open: sel
  Register #(.width(32)) IR (
    .D(rom_1_data), .en(rom_3_data[0]), .Q({out_8, RD, RA, IR_q, out_2}), .clk(clock_1_out),
    .clr(button_1_out));
  not not_1 (not_1_out, and_1_out);
  and and_1 (and_1_out, out_8[1], out_8[0]);
  Multiplexer #(.width(5), .enable("false")) multiplexer_1 (
    .in0(RD), .in1({IR_q, out_2[15:14]}), .out(RB), .sel(not_1_out));
  ROM #(.addrWidth(9), .dataWidth(5)) rom_2 (
    .addr({register_1_q, out_8, comparator_1_eq[0]}), .data(rom_2_data));  // open: sel
  Register #(.width(5)) register_1 (
    .D(rom_2_data), .Q(register_1_q), .clk(clock_1_out), .clr(button_1_out));  // open: en
  BR32 br32_1 (
    .busW(out_4), .RegWr(rom_3_data[12]), .RA(RA), .RB(RB), .RW(RD), .busA(br32_1_busa), .busB(br32_1_busb),
    .CLK(clock_1_out));
  assign bit_extender_1_out = {{16{out_2[15]}}, out_2};  // Bit_Extender bit_extender_1
  Register #(.width(32)) u_RA (
    .D(br32_1_busa), .en(rom_3_data[10]), .Q({RA_q, out_3}), .clk(clock_1_out), .clr(button_1_out));
  Register #(.width(32)) u_RB (
    .D(br32_1_busb), .en(rom_3_data[11]), .Q({RB_q_2, RB_q}), .clk(clock_1_out), .clr(button_1_out));
  ROM #(.addrWidth(5), .dataWidth(13)) rom_3 (.addr(register_1_q), .data(rom_3_data));  // open: sel
  Adder #(.width(32)) adder_1 (.a({RA_q, out_3}), .b({RB_q_2, RB_q}), .out(out_1));  // open: cin, cout
  Comparator #(.width(32)) comparator_1 (
    .a({RA_q, out_3}), .b({RB_q_2, RB_q}), .eq(comparator_1_eq[0]));  // open: gt, lt
  not not_2 (not_2_out, rom_3_data[7]);
  Register #(.width(32)) RC (.D(out_1), .en(rom_3_data[9]), .Q(RC_q), .clk(clock_1_out), .clr(button_1_out));
  Multiplexer #(.width(32), .enable("false")) multiplexer_2 (
    .in0(RC_q), .in1(multiplexer_3_out), .out(out_4), .sel(rom_3_data[8]));
  Register #(.width(32)) RMEM (.D(ram_1_data), .en(rom_3_data[3]), .Q(RMEM_q), .clk(clock_1_out), .clr(button_1_out));
  RAM #(.addrWidth(16), .dataWidth(32), .bus("separate")) ram_1 (
    .addr(out_3), .din({RB_q_2, RB_q}), .data(ram_1_data), .str(not_2_out), .sel(rom_3_data[1]),
    .clk(clock_1_out), .ld(rom_3_data[7]));  // open: clr
  Multiplexer #(.width(32), .enable("false")) multiplexer_3 (
    .in0(RMEM_q), .in1(bit_extender_1_out), .out(multiplexer_3_out), .sel(rom_3_data[5]));
  // tty_ctrl tty_ctrl_1: pin names not known; wires that end beside it: button_1_out
  // TTY tty_1: pin names not known; wires that end beside it: out_3, rom_3_data[6], RB_q, clock_1_out

  // Notes on the sheet:
  //   contents of rom_1 (hex, n*v repeats v):
  //   40000000 41000001 4200004a 43000000 44000000 45000000 46000006 23100000 2088000 4190000 5094000
  //   80010000 6530000e 60000007 47000050 28380000 4900ffff 68200040 4a00004e 804a8000 4a00004f 804a8000
  //   60000fff 41*0 4a00004f 804a8000 4a00004b 804a8000 60000fff 4026*0 60000fff
  //   K
  //   contents of rom_2 (hex, n*v repeats v):
  //   12*1 4*0 3 3 6 6 2 2 b b 9 9 22*0 4 4 14*0 5 5 32*0 7 7 14*0 8 8 36*0 a a 12*0 b b 0 0 b b 10*0 c c
  //   15*0 d
  //   CONTROL UNIT
  //   contents of rom_3 (hex, n*v repeats v):
  //   11 0 1120 c00 1200 1000 400 8a 1100 c00 42 c00 0 5
  //   RESET CABLE
  //   CLOCK CABLE
endmodule
