// Logisim project NIA-seg.circ as structural Verilog: 3 circuits, main circuit BR4
module BR4 (
  input  RegWR,
  input  [1:0] RA,
  input  [1:0] RB,
  input  CLEAR,
  input  [1:0] RW,
  input  [31:0] busW,
  input  clk,
  output [31:0] busA,
  output [31:0] busB
);

  wire and_1_out, and_2_out, and_3_out, and_4_out, decoder_1_out0, decoder_1_out1, decoder_1_out2,
       decoder_1_out3;
  wire [31:0] register_1_q, register_2_q, register_3_q, register_4_q;

  Decoder #(.select(2), .enable("false")) decoder_1 (
    .out0(decoder_1_out0), .out1(decoder_1_out1), .out2(decoder_1_out2), .out3(decoder_1_out3), .sel(RW));
  and and_1 (and_1_out, RegWR, decoder_1_out0);
  and and_2 (and_2_out, RegWR, decoder_1_out1);
  and and_3 (and_3_out, RegWR, decoder_1_out2);
  and and_4 (and_4_out, RegWR, decoder_1_out3);
  Register #(.width(32)) register_1 (.D(busW), .en(and_1_out), .Q(register_1_q), .clk(clk), .clr(CLEAR));
  Register #(.width(32)) register_2 (.D(busW), .en(and_2_out), .Q(register_2_q), .clk(clk), .clr(CLEAR));
  Register #(.width(32)) register_3 (.D(busW), .en(and_3_out), .Q(register_3_q), .clk(clk), .clr(CLEAR));
  Register #(.width(32)) register_4 (.D(busW), .en(and_4_out), .Q(register_4_q), .clk(clk), .clr(CLEAR));
  Multiplexer #(.select(2), .width(32), .enable("false")) multiplexer_1 (
    .in0(register_1_q), .in1(register_2_q), .in2(register_3_q), .in3(register_4_q), .out(busA), .sel(RA));
  Multiplexer #(.select(2), .width(32), .enable("false")) multiplexer_2 (
    .in0(register_1_q), .in1(register_2_q), .in2(register_3_q), .in3(register_4_q), .out(busB), .sel(RB));
endmodule

module BR32 (
  input  [31:0] busW,
  input  RegWr,
  input  [4:0] RA,
  input  [4:0] RB,
  input  [4:0] RW,
  input  CLK,
  output [31:0] busA,
  output [31:0] busB
);

  wire CLEAR_out, decoder_1_out0, decoder_1_out1, decoder_1_out2, decoder_1_out3, decoder_1_out4,
       decoder_1_out5, decoder_1_out6, decoder_1_out7;
  wire [31:0] br4_1_busa, br4_1_busb, br4_2_busa, br4_2_busb, br4_3_busa, br4_3_busb, br4_4_busa, br4_4_busb,
       br4_5_busa, br4_5_busb, br4_6_busa, br4_6_busb, br4_7_busa, br4_7_busb, br4_8_busa;

  Decoder #(.select(3), .disabled(0)) decoder_1 (
    .out0(decoder_1_out0), .out1(decoder_1_out1), .out2(decoder_1_out2), .out3(decoder_1_out3),
    .out4(decoder_1_out4), .out5(decoder_1_out5), .out6(decoder_1_out6), .out7(decoder_1_out7),
    .sel(RW[4:2]), .en(RegWr));
  BR4 br4_1 (
    .RegWR(decoder_1_out0), .RW(RW[1:0]), .busW(busW), .busA(br4_1_busa), .busB(br4_1_busb), .RA(RA[1:0]),
    .RB(RB[1:0]), .clk(CLK), .CLEAR(CLEAR_out));
  BR4 br4_2 (
    .RegWR(decoder_1_out1), .RW(RW[1:0]), .busW(busW), .busA(br4_2_busa), .busB(br4_2_busb), .RA(RA[1:0]),
    .RB(RB[1:0]), .clk(CLK), .CLEAR(CLEAR_out));
  BR4 br4_3 (
    .RegWR(decoder_1_out2), .RW(RW[1:0]), .busW(busW), .busA(br4_3_busa), .busB(br4_3_busb), .RA(RA[1:0]),
    .RB(RB[1:0]), .clk(CLK), .CLEAR(CLEAR_out));
  BR4 br4_4 (
    .RegWR(decoder_1_out3), .RW(RW[1:0]), .busW(busW), .busA(br4_4_busa), .busB(br4_4_busb), .RA(RA[1:0]),
    .RB(RB[1:0]), .clk(CLK), .CLEAR(CLEAR_out));
  BR4 br4_5 (
    .RegWR(decoder_1_out4), .RW(RW[1:0]), .busW(busW), .busA(br4_5_busa), .busB(br4_5_busb), .RA(RA[1:0]),
    .RB(RB[1:0]), .clk(CLK), .CLEAR(CLEAR_out));
  BR4 br4_6 (
    .RegWR(decoder_1_out5), .RW(RW[1:0]), .busW(busW), .busA(br4_6_busa), .busB(br4_6_busb), .RA(RA[1:0]),
    .RB(RB[1:0]), .clk(CLK), .CLEAR(CLEAR_out));
  BR4 br4_7 (
    .RegWR(decoder_1_out6), .RW(RW[1:0]), .busW(busW), .busA(br4_7_busa), .busB(br4_7_busb), .RA(RA[1:0]),
    .RB(RB[1:0]), .clk(CLK), .CLEAR(CLEAR_out));
  BR4 br4_8 (
    .RegWR(decoder_1_out7), .RW(RW[1:0]), .busW(busW), .busA(br4_8_busa), .busB(br4_8_busa), .RA(RA[1:0]),
    .RB(RB[1:0]), .clk(CLK), .CLEAR(CLEAR_out));
  Button CLEAR (.out(CLEAR_out));
  Multiplexer #(.select(3), .width(32), .enable("false")) multiplexer_1 (
    .in0(br4_1_busa), .in1(br4_2_busa), .in2(br4_3_busa), .in3(br4_4_busa), .in4(br4_5_busa),
    .in5(br4_6_busa), .in6(br4_7_busa), .in7(br4_8_busa), .out(busA), .sel(RA[4:2]));
  Multiplexer #(.select(3), .width(32), .enable("false")) multiplexer_2 (
    .in0(br4_1_busb), .in1(br4_2_busb), .in2(br4_3_busb), .in3(br4_4_busb), .in4(br4_5_busb),
    .in5(br4_6_busb), .in6(br4_7_busb), .in7(br4_8_busa), .out(busB), .sel(RB[4:2]));
endmodule

module CPU (
  output [15:0] out_1,
  output [4:0] RA,
  output [4:0] RB,
  output [4:0] RD,
  output [2:0] out_5
);

  wire and_1_out, and_2_out, button_1_out, clock_1_out, comparator_1_eq, not_1_out, not_2_out, not_3_out,
       not_4_out;
  wire [4:0] DESTINO_2_q, DESTINO_3_q, DESTINO_q, rom_2_data, SIGNAL_3_q, SIGNAL_q, tty_1_p2;
  wire [15:0] COUNTER_q, tty_1_p1;
  wire [18:16] ID_q;
  wire [31:0] adder_1_out, ALU_2_q, ALU_q, BANCO_busa, BANCO_busb, bit_extender_1_out, K_2_q, K_3_q, K_q,
       multiplexer_2_out, multiplexer_3_out, RA_q, ram_1_data, RB_q, RMEM_q, rom_1_data, tty_1_p3;

  and and_1 (and_1_out, comparator_1_eq, not_1_out, and_2_out);
  not not_1 (not_1_out, out_5[2]);
  Counter #(.width(16), .max('hffff), .ongoal("load")) COUNTER (
    .load(and_1_out), .D(out_1), .count(not_2_out), .Q(COUNTER_q), .clk(clock_1_out), .clr(button_1_out));  // open: carry
  not not_2 (not_2_out, and_1_out);
  Clock clock_1 (.out(clock_1_out));
  Button button_1 (.out(button_1_out));
  ROM #(.addrWidth(16), .dataWidth(32)) rom_1 (.addr(COUNTER_q), .data(rom_1_data));  // open: sel
  Register #(.width(32)) ID (
    .D(rom_1_data), .en(1'b1), .Q({out_5, RD, RA, ID_q, out_1}), .clk(clock_1_out), .clr(button_1_out));
  not not_3 (not_3_out, and_2_out);
  and and_2 (and_2_out, out_5[1], out_5[0]);
  ROM #(.addrWidth(3), .dataWidth(5)) rom_2 (.addr(out_5), .data(rom_2_data));  // open: sel
  Multiplexer #(.width(5), .enable("false")) multiplexer_1 (
    .in0(RD), .in1({ID_q, out_1[15:14]}), .out(RB), .sel(not_3_out));
  LED WRITING (.in(SIGNAL_3_q[4]));
  assign bit_extender_1_out = {{16{out_1[15]}}, out_1};  // Bit_Extender bit_extender_1
  BR32 BANCO (
    .busW(multiplexer_2_out), .RegWr(SIGNAL_3_q[4]), .RA(RA), .RB(RB), .RW(DESTINO_3_q), .busA(BANCO_busa),
    .busB(BANCO_busb), .CLK(clock_1_out));
  // tty_ctrl tty_ctrl_1: pin names not known
  // TTY tty_1: pin names not known; wires that end beside it: tty_1_p1, tty_1_p2[0], tty_1_p3[6:0], clock_1_out
  Register #(.width(32)) K (.D(bit_extender_1_out), .en(1'b1), .Q(K_q), .clk(clock_1_out), .clr(button_1_out));
  Register #(.width(32)) u_RA (.D(BANCO_busa), .en(1'b1), .Q(RA_q), .clk(clock_1_out), .clr(button_1_out));
  Register #(.width(32)) u_RB (.D(BANCO_busb), .en(1'b1), .Q(RB_q), .clk(clock_1_out), .clr(button_1_out));
  Register #(.width(5)) SIGNAL (.D(rom_2_data), .en(1'b1), .Q(SIGNAL_q), .clk(clock_1_out), .clr(button_1_out));
  Register #(.width(5)) DESTINO (.D(RD), .en(1'b1), .Q(DESTINO_q), .clk(clock_1_out), .clr(button_1_out));
  Adder #(.width(32)) adder_1 (.a(RA_q), .b(RB_q), .out(adder_1_out));  // open: cin, cout
  Register #(.width(32)) K_2 (.D(K_q), .en(1'b1), .Q(K_2_q), .clk(clock_1_out), .clr(button_1_out));
  Register #(.width(16)) RA_2 (.D(RA_q[15:0]), .en(1'b1), .Q(tty_1_p1), .clk(clock_1_out), .clr(button_1_out));
  Register #(.width(32)) ALU (.D(adder_1_out), .en(1'b1), .Q(ALU_q), .clk(clock_1_out), .clr(button_1_out));
  Register #(.width(32)) RB_2 (.D(RB_q), .en(1'b1), .Q(tty_1_p3), .clk(clock_1_out), .clr(button_1_out));
  Register #(.width(5)) SIGNAL_2 (.D(SIGNAL_q), .en(1'b1), .Q(tty_1_p2), .clk(clock_1_out), .clr(button_1_out));
  Register #(.width(5)) DESTINO_2 (.D(DESTINO_q), .en(1'b1), .Q(DESTINO_2_q), .clk(clock_1_out), .clr(button_1_out));
  Multiplexer #(.width(32), .enable("false")) multiplexer_2 (
    .in0(ALU_2_q), .in1(multiplexer_3_out), .out(multiplexer_2_out), .sel(SIGNAL_3_q[3]));
  Register #(.width(5)) SIGNAL_3 (.D(tty_1_p2), .en(1'b1), .Q(SIGNAL_3_q), .clk(clock_1_out), .clr(button_1_out));
  Register #(.width(5)) DESTINO_3 (.D(DESTINO_2_q), .en(1'b1), .Q(DESTINO_3_q), .clk(clock_1_out), .clr(button_1_out));
  Comparator #(.width(32)) comparator_1 (.a(BANCO_busa), .b(BANCO_busb), .eq(comparator_1_eq));  // open: gt, lt
  not not_4 (not_4_out, tty_1_p2[1]);
  RAM #(.addrWidth(16), .dataWidth(32), .bus("separate")) ram_1 (
    .addr(tty_1_p1), .din(tty_1_p3), .data(ram_1_data), .str(not_4_out), .sel(tty_1_p2[0]),
    .clk(clock_1_out), .ld(tty_1_p2[1]));  // open: clr
  Register #(.width(32)) K_3 (.D(K_2_q), .en(1'b1), .Q(K_3_q), .clk(clock_1_out), .clr(button_1_out));
  Register #(.width(32)) ALU_2 (.D(ALU_q), .en(1'b1), .Q(ALU_2_q), .clk(clock_1_out), .clr(button_1_out));
  Register #(.width(32)) RMEM (.D(ram_1_data), .en(1'b1), .Q(RMEM_q), .clk(clock_1_out), .clr(button_1_out));
  Multiplexer #(.width(32), .enable("false")) multiplexer_3 (
    .in0(RMEM_q), .in1(K_3_q), .out(multiplexer_3_out), .sel(SIGNAL_3_q[2]));

  // Notes on the sheet:
  //   contents of rom_1 (hex, n*v repeats v):
  //   40000000 41000001 4200004a 43000000 44000000 45000000 46000006 23100000 2088000 e0000000 e0000000
  //   4190000 5094000 e0000000 e0000000 80010000 e0000000 e0000000 65300018 e0000000 e0000000 60000007
  //   e0000000 e0000000 47000050 e0000000 e0000000 e0000000 28380000 4900ffff e0000000 e0000000 6820005c
  //   e0000000 e0000000 4a00004e e0000000 e0000000 e0000000 804a8000 4a00004f e0000000 e0000000 e0000000
  //   804a8000 e0000000 e0000000 e0000000 60000fff e0000000 e0000000 41*0 4a00004f e0000000 e0000000
  //   e0000000 804a8000 4a00004b e0000000 e0000000 e0000000 804a8000 e0000000 e0000000 60000fff e0000000
  //   e0000000 4026*0 60000fff
  //   CONTROL UNIT
  //   K
  //   contents of rom_2 (hex, n*v repeats v):
  //   10 1b 1c 0 1
  //   EX
  //   MEM
  //   RESET CABLE
  //   CLOCK CABLE
  //   WB
endmodule
